// Logisim project cpu24.circ as structural Verilog: 11 circuits, main circuit ◇单周期MIPS
module \单周期MIPS  (
  output RegWrite,
  output MemWrite,
  output [31:0] PC,
  output [31:0] IR,
  output [31:0] RDin,
  output [31:0] MDin
);

  wire and_2_out, and_3_out, Beq, beq_bne_suc, BGTZ, bgtz_suc, Bne, CLK, comparator_2_eq, equal, Go, IR1,
       IR2, IR3, isI, isJ, isRTYPE, JAL, JMP, JR, LB, not_1_out, not_2_out, or_1_out, or_3_out, or_4_out,
       or_5_out, pause, SignedExt, stop, Syscall, W1, W2, W3, \单周期硬布线控制器_1_alu_src , \单周期硬布线控制器_1_memtoreg ,
       \单周期硬布线控制器_1_regdst ;
  wire [1:0] index, \确定pc_1_out_7 ;
  wire [3:0] \单周期硬布线控制器_1_alu_op ;
  wire [4:0] multiplexer_3_out, multiplexer_4_out, multiplexer_5_out, multiplexer_6_out, multiplexer_10_out;
  wire [7:0] LBans;
  wire [15:0] \总周期数 , \无条件分支数 , \条件分支成功数 ;
  wire [27:0] nextpc;
  wire [31:0] bit_extender_1_out, bit_extender_2_out, LedData, multiplexer_1_out, multiplexer_2_out,
       multiplexer_8_out, multiplexer_9_out, multiplexer_12_out, pcbranch, R1data, ram_1_data, shifter_1_out;
  wire [31:2] mips_alu_1_result;
  wire [31:28] jmppc;

  Clock #(.highDuration(1), .lowDuration(1)) clock_1 (.out(CLK));
  Button _1 (.out(IR1));
  Button _2 (.out(IR2));
  Button _3 (.out(IR3));
  or or_1 (or_1_out, JMP, JAL);
  Button \u_继续运行  (.out(Go));
  LED #(.active("true")) led_1 (.in(W1));
  LED #(.active("true")) led_2 (.in(W2));
  LED #(.active("true")) led_3 (.in(W3));
  Hex_Digit_Display hex_digit_display_1 (.value(LedData[31:28]));  // open: dp
  \确定pc  \u_确定pc_1  (
    .equal(equal), .Beq(Beq), .Bne(Bne), .JR(JR), .j(or_1_out), .out_7(\确定pc_1_out_7 ),
    .beq_bne_suc(beq_bne_suc));
  and and_1 (bgtz_suc, BGTZ, not_1_out);
  Multiplexer #(.select(2), .width(32), .disabled("Z"), .enable("false")) multiplexer_1 (
    .in0(pcbranch), .in1({jmppc, nextpc}), .in2(R1data), .in3({jmppc, IR[25:0], 2'b00}),
    .out(multiplexer_1_out), .sel(\确定pc_1_out_7 ));
  D_Flip_Flop #(.trigger("falling"), .Pre_Clr_Positions("ABOVE_BELOW"), .NegatePresetClear("false"), .enable("false"), .NewFFLayout("true")) d_ff_1 (
    .clk(CLK), .D(pause), .Qn(stop), .reset(Go));  // open: Q, preset
  Hex_Digit_Display hex_digit_display_2 (.value(LedData[23:20]));  // open: dp
  Hex_Digit_Display hex_digit_display_3 (.value(LedData[27:24]));  // open: dp
  not not_1 (not_1_out, RDin[0]);
  Multiplexer #(.select(1), .width(32), .disabled("Z"), .enable("false")) multiplexer_2 (
    .in0(multiplexer_1_out), .in1(pcbranch), .out(multiplexer_2_out), .sel(bgtz_suc));
  Register #(.width(32), .trigger("rising"), .Select("low")) u_PC (
    .D(multiplexer_2_out), .en(stop), .Q(PC), .clk(CLK));  // open: clr
  Hex_Digit_Display hex_digit_display_4 (.value(LedData[15:12]));  // open: dp
  Hex_Digit_Display hex_digit_display_5 (.value(LedData[19:16]));  // open: dp
  Hex_Digit_Display hex_digit_display_6 (.value(LedData[11:8]));  // open: dp
  Hex_Digit_Display hex_digit_display_7 (.value(LedData[7:4]));  // open: dp
  // Probe on \总周期数 
  Adder #(.width(32)) adder_1 (.a(PC), .b(32'h4), .out({jmppc, nextpc}));  // open: cin, cout
  Hex_Digit_Display hex_digit_display_8 (.value(LedData[3:0]));  // open: dp
  Counter #(.width(16), .max('hffff), .ongoal("wrap"), .trigger("rising"), .behavior("new")) counter_1 (
    .count(stop), .Q(\总周期数 ), .clk(CLK));  // open: load, D, carry, clr, preset, down
  Comparator #(.width(6), .mode("unsigned")) comparator_1 (.a({6{1'b0}}), .b(IR[31:26]), .eq(isRTYPE));  // open: gt, lt
  ROM #(.addrWidth(10), .dataWidth(32), .Select("high")) rom_1 (.addr(PC[11:2]), .data(IR));
  \单周期硬布线控制器  \u_单周期硬布线控制器_1  (
    .Func(IR[5:0]), .OP(IR[31:26]), .ALU_OP(\单周期硬布线控制器_1_alu_op ), .MemToReg(\单周期硬布线控制器_1_memtoreg ),
    .MemWrite(MemWrite), .ALU_SRC(\单周期硬布线控制器_1_alu_src ), .RegWrite(RegWrite), .SysCALL(Syscall),
    .SignedExt(SignedExt), .RegDst(\单周期硬布线控制器_1_regdst ), .JR(JR), .JMP(JMP), .Beq(Beq), .JAL(JAL),
    .Bne(Bne), .BGTZ(BGTZ), .LB(LB));
  Multiplexer #(.select(1), .width(5), .disabled("Z"), .enable("false")) multiplexer_3 (
    .in0(IR[20:16]), .in1(IR[15:11]), .out(multiplexer_3_out), .sel(\单周期硬布线控制器_1_regdst ));
  Multiplexer #(.select(1), .width(5), .disabled("Z"), .enable("false")) multiplexer_4 (
    .in0(multiplexer_3_out), .in1({5{1'b1}}), .out(multiplexer_4_out), .sel(JAL));
  and and_2 (and_2_out, SignedExt, IR[15]);
  Comparator #(.width(32), .mode("unsigned")) comparator_2 (
    .a(MDin), .b(32'h22), .eq(comparator_2_eq));  // open: gt, lt
  Multiplexer #(.select(1), .width(5), .disabled("Z"), .enable("false")) multiplexer_5 (
    .in0(IR[25:21]), .in1(5'b00100), .out(multiplexer_5_out), .sel(Syscall));
  Multiplexer #(.select(1), .width(5), .disabled("Z"), .enable("false")) multiplexer_6 (
    .in0(IR[20:16]), .in1(5'b00010), .out(multiplexer_6_out), .sel(Syscall));
  assign bit_extender_1_out = {{16{and_2_out}}, IR[15:0]};  // Bit_Extender bit_extender_1
  Multiplexer #(.select(1), .width(32), .disabled("Z"), .enable("false")) multiplexer_7 (
    .in0(multiplexer_9_out), .in1({jmppc, nextpc}), .out(RDin), .sel(JAL));
  not not_2 (not_2_out, comparator_2_eq);
  MIPS_Regifile mips_regifile_1 (
    .Din(RDin), .Clk(CLK), .R1(R1data), .R2(MDin), .WE(RegWrite), .W_num(multiplexer_4_out),
    .R1_num(multiplexer_5_out), .R2_num(multiplexer_6_out));
  Shifter #(.width(32), .shift("ll")) shifter_1 (.in(bit_extender_1_out), .\dist (5'b00010), .out(shifter_1_out));
  and and_3 (and_3_out, Syscall, comparator_2_eq);
  and and_4 (pause, Syscall, not_2_out);
  Multiplexer #(.select(1), .width(32), .disabled("Z"), .enable("false")) multiplexer_8 (
    .in0(MDin), .in1(bit_extender_1_out), .out(multiplexer_8_out), .sel(\单周期硬布线控制器_1_alu_src ));
  Multiplexer #(.select(1), .width(32), .disabled("Z"), .enable("false")) multiplexer_9 (
    .in0(multiplexer_12_out), .in1(bit_extender_2_out), .out(multiplexer_9_out), .sel(LB));
  or or_2 (isJ, JMP, JAL);
  or or_3 (or_3_out, isJ, isRTYPE, Syscall);
  Multiplexer #(.select(1), .width(5), .disabled("Z"), .enable("false")) multiplexer_10 (
    .in0({5{1'b0}}), .in1(IR[10:6]), .out(multiplexer_10_out), .sel(isRTYPE));
  Adder #(.width(32)) adder_2 (.a(shifter_1_out), .b({jmppc, nextpc}), .out(pcbranch));  // open: cin, cout
  Register #(.width(32), .trigger("rising"), .Select("low")) register_1 (
    .D(R1data), .en(and_3_out), .Q(LedData), .clk(CLK));  // open: clr
  not not_3 (isI, or_3_out);
  MIPS_ALU mips_alu_1 (
    .X(R1data), .Y(multiplexer_8_out), .AluOP(\单周期硬布线控制器_1_alu_op ), .Equal(equal),
    .Result({mips_alu_1_result, index}), .shamt(multiplexer_10_out));  // open: Result_2
  or or_4 (or_4_out, JMP, JR, JAL);
  assign bit_extender_2_out = {{24{multiplexer_12_out[31]}}, LBans};  // Bit_Extender bit_extender_2
  Counter #(.width(16), .max('hffff), .ongoal("wrap"), .trigger("rising"), .behavior("old")) counter_2 (
    .count(or_4_out), .Q(\无条件分支数 ), .clk(CLK));  // open: load, D, carry, clr, preset
  Counter #(.width(16), .max('hffff), .ongoal("wrap"), .trigger("rising"), .behavior("old")) counter_3 (
    .count(or_5_out), .Q(\条件分支成功数 ), .clk(CLK));  // open: load, D, carry, clr, preset
  or or_5 (or_5_out, beq_bne_suc, bgtz_suc);
  RAM #(.addrWidth(10), .dataWidth(32), .bus("separate"), .Select("high")) ram_1 (
    .addr(mips_alu_1_result[11:2]), .din(MDin), .data(ram_1_data), .str(MemWrite), .clk(CLK));  // open: sel, ld, clr
  Multiplexer #(.select(2), .width(8), .disabled("Z"), .enable("false")) multiplexer_11 (
    .in0(multiplexer_12_out[7:0]), .in1(multiplexer_12_out[15:8]), .in2(multiplexer_12_out[23:16]),
    .in3(multiplexer_12_out[31:24]), .out(LBans), .sel(index));
  Multiplexer #(.select(1), .width(32), .disabled("Z"), .enable("false")) multiplexer_12 (
    .in0({mips_alu_1_result, index}), .in1(ram_1_data), .out(multiplexer_12_out), .sel(\单周期硬布线控制器_1_memtoreg ));

  // Other names for the same wires on the sheet: address[25:0] = IR[25:0]; jmppc[27:2] = IR[25:0];
  //   shamt[4:0] = IR[10:6]; nextpc[31:28] = jmppc; R2data[31:0] = MDin

  // Notes on the sheet:
  //   中断源
  //   中断等待指示
  //   总复位信号应将除ROM以外所有存储组件全部清零
  //   数码管输出
  //   数码管输出应该用寄存器锁存，否则显示数据只能一闪而过
  //   指令存储器
  //   指令字
  //   contents of rom_1 (hex, n*v repeats v):
  //   20110001 8100005 20110001 20120002 20130003 8100009 20110001 20120002 20130003 810000d 20110001
  //   20120002 20130003 8100011 20110001 20120002 20130003 c1000f4 20100001 20110001 118fc0 112020
  //   20020022 c 118882 12200001 8100015 112020 20020022 c 20110001 118880 112020 20020022 c 12200001
  //   810001f 20110001 118fc0 112020 20020022 c 1188c3 112020 20020022 c 118903 112020 20020022 c 118903
  //   112020 20020022 c 118903 112020 20020022 c 118903 112020 20020022 c 118903 112020 20020022 c 118903
  //   112020 20020022 c 118903 112020 20020022 c 20100001 109fc0 139fc3 8021 2012000c 24160003 26100001
  //   3210000f 20080008 20090001 139900 2709825 132020 20020022 c 1094022 1500fff9 22100001 2018000f
  //   2188024 108700 20080008 20090001 139902 2709825 132021 20020022 c 1094022 1500fff9 108702 2c9b022
  //   12c00001 8100050 4020 1084027 84400 3508ffff 82021 20020022 c 2010ffff 20110000 ae300000 22100001
  //   22310004 ae300000 22100001 22310004 ae300000 22100001 22310004 ae300000 22100001 22310004 ae300000
  //   22100001 22310004 ae300000 22100001 22310004 ae300000 22100001 22310004 ae300000 22100001 22310004
  //   ae300000 22100001 22310004 ae300000 22100001 22310004 ae300000 22100001 22310004 ae300000 22100001
  //   22310004 ae300000 22100001 22310004 ae300000 22100001 22310004 ae300000 22100001 22310004 ae300000
  //   22100001 22310004 22100001 8020 2011003c 8e130000 8e340000 274402a 11000002 ae330000 ae140000
  //   2231fffc 1611fff8 102020 20020022 c 22100004 2011003c 1611fff2 20020032 c 2008ffff 20117777 112020
  //   20020022 c 200b0010 2288826 112020 20020022 c 216bffff 1560fffa 2002000a c 2008ffff 20090000
  //   20111997 112020 20020022 c 2288820 2e291949 1120fffa 2002000a c 20090000 200b0010 34118483 20120404
  //   118c00 129400 36318281 22520404 ad310000 2328820 21290004 216bffff 1560fffb 200b0020 20090000
  //   81310000 112020 20020022 c 21290001 216bffff 1560fff9 2002000a c 2011000f 112020 20020022 c 2231ffff
  //   1e20fffb 2002000a c 8100000 2002000a c 20100000 22100001 102020 20020022 c 22100002 102020 20020022
  //   c 22100003 102020 20020022 c 22100004 102020 20020022 c 22100005 102020 20020022 c 22100006 102020
  //   20020022 c 22100007 102020 20020022 c 22100008 102020 20020022 20020022 c 3e00008
  //   rd
  //   JMP
  //   JR
  //   OP
  //   OP
  //   Func
  //   Func
  //   rs
  //   rt
  //   rd
  //   Beq
  //   Bne
  //   MemToReg
  //   MemWrite
  //   AluOP
  //   AluSrcB
  //   RegWrite
  //   JAL
  //   RegDst
  //   Syscall
  //   为方便自动评测，需要输出PC，IR，寄存器文件写入端口RDin，内存写入端口MDin等信号
  //   j型指令
  //   I型指令
endmodule

// 单周期硬布线控制器
module \单周期硬布线控制器  (
  input  [5:0] OP,
  input  [5:0] Func,
  output [3:0] ALU_OP,
  output MemToReg,
  output MemWrite,
  output ALU_SRC,
  output RegWrite,
  output SysCALL,
  output SignedExt,
  output RegDst,
  output Beq,
  output Bne,
  output JR,
  output JMP,
  output JAL,
  output BGTZ,
  output LB
);

  \运算控制器自动生成  \u_运算控制器自动生成_1  (
    .OP0(OP[0]), .OP1(OP[1]), .OP2(OP[2]), .OP3(OP[3]), .OP4(OP[4]), .OP5(OP[5]), .F0(Func[0]), .F1(Func[1]),
    .F2(Func[2]), .F3(Func[3]), .F4(Func[4]), .F5(Func[5]), .S0(ALU_OP[0]), .S1(ALU_OP[1]), .S2(ALU_OP[2]),
    .S3(ALU_OP[3]));
  \控制信号自动生成  \u_控制信号自动生成_1  (
    .OP0(OP[0]), .OP1(OP[1]), .OP2(OP[2]), .OP3(OP[3]), .OP4(OP[4]), .OP5(OP[5]), .F0(Func[0]), .F1(Func[1]),
    .F2(Func[2]), .F3(Func[3]), .F4(Func[4]), .F5(Func[5]), .MemToReg(MemToReg), .MemWrite(MemWrite),
    .ALU_SRC(ALU_SRC), .RegWrite(RegWrite), .SysCALL(SysCALL), .SignedExt(SignedExt), .RegDst(RegDst),
    .BEQ(Beq), .BNE(Bne), .JR(JR), .JUMP(JMP), .JAL(JAL), .BGTZ(BGTZ), .LB(LB));

  // Other names for the same wires on the sheet: OP_CODE[5:0] = OP

  // Notes on the sheet:
  //   运算器控制器，根据指令生成运算器功能选择信号
  //   控制信号生成，产生数据通路需要的其他控制信号
endmodule

// 运算器控制器
module \运算控制器自动生成  (
  input  OP0,
  input  OP1,
  input  OP2,
  input  OP3,
  input  OP4,
  input  OP5,
  input  F0,
  input  F1,
  input  F2,
  input  F3,
  input  F4,
  input  F5,
  output S0,
  output S1,
  output S2,
  output S3
);

  wire and_1_out, and_2_out, and_3_out, and_4_out, and_5_out, and_6_out, and_7_out, and_8_out, and_9_out,
       and_10_out, and_11_out, and_12_out, and_13_out, and_14_out, and_15_out, and_16_out, and_17_out,
       and_18_out, and_19_out, and_20_out, and_21_out, and_22_out, and_23_out, and_24_out, and_25_out,
       and_26_out, and_27_out, and_28_out, and_29_out, and_30_out, and_31_out, and_32_out, and_33_out,
       and_34_out, and_35_out, and_36_out, and_37_out, and_38_out, and_39_out, and_40_out, and_41_out,
       and_42_out, and_43_out, and_44_out, and_45_out, and_46_out, and_47_out, and_48_out, and_49_out,
       not_1_out, not_2_out, not_3_out, not_4_out, not_5_out, not_6_out, not_7_out, not_8_out, not_9_out,
       not_10_out, not_11_out, not_12_out, not_13_out, not_14_out, not_15_out, not_16_out, not_17_out,
       not_18_out, not_19_out, not_20_out, not_21_out, not_22_out, not_23_out, not_24_out, not_25_out,
       not_26_out, not_27_out, not_28_out, not_29_out, not_30_out, not_31_out, not_32_out, not_33_out,
       not_34_out, not_35_out, not_36_out, not_37_out, not_38_out, not_39_out, not_40_out, not_41_out,
       not_42_out, not_43_out, not_44_out, not_45_out, not_46_out, not_47_out, not_48_out, not_49_out,
       not_50_out, not_51_out, not_52_out, not_53_out, not_54_out, not_55_out, not_56_out, not_57_out,
       not_58_out, not_59_out, not_60_out, not_61_out, not_62_out, not_63_out, not_64_out, not_65_out,
       not_66_out, not_67_out, not_68_out, not_69_out, not_70_out, not_71_out, not_72_out, not_73_out,
       not_74_out, not_75_out, not_76_out, not_77_out, not_78_out, not_79_out, not_80_out, not_81_out,
       not_82_out, not_83_out, not_84_out, not_85_out, not_86_out, not_87_out, not_88_out, not_89_out,
       not_90_out, not_91_out, not_92_out, not_93_out, not_94_out, not_95_out, not_96_out, not_97_out,
       not_98_out, not_99_out, not_100_out, not_101_out, not_102_out, not_103_out, not_104_out, not_105_out,
       not_106_out, not_107_out, not_108_out, not_109_out, not_110_out, not_111_out, not_112_out,
       not_113_out, not_114_out, not_115_out, not_116_out, not_117_out, not_118_out, not_119_out,
       not_120_out, not_121_out, not_122_out, not_123_out, not_124_out, not_125_out, not_126_out,
       not_127_out, not_128_out, not_129_out, not_130_out, not_131_out, not_132_out, not_133_out,
       not_134_out, not_135_out, not_136_out, not_137_out, not_138_out, not_139_out, not_140_out,
       not_141_out, not_142_out, not_143_out, not_144_out, not_145_out, not_146_out, not_147_out,
       not_148_out, not_149_out, not_150_out, not_151_out, not_152_out, not_153_out, not_154_out,
       not_155_out, not_156_out, not_157_out, not_158_out, not_159_out, not_160_out, not_161_out,
       not_162_out, not_163_out, not_164_out, not_165_out, not_166_out, not_167_out, not_168_out,
       not_169_out, not_170_out, not_171_out, not_172_out, not_173_out, not_174_out, not_175_out,
       not_176_out, not_177_out, not_178_out, not_179_out, not_180_out, not_181_out, not_182_out,
       not_183_out, not_184_out, not_185_out, not_186_out, not_187_out, not_188_out, not_189_out,
       not_190_out, not_191_out, not_192_out, not_193_out, not_194_out, not_195_out, not_196_out,
       not_197_out, not_198_out, not_199_out, not_200_out, not_201_out, not_202_out, not_203_out,
       not_204_out, not_205_out, not_206_out, not_207_out, not_208_out, not_209_out, not_210_out,
       not_211_out, not_212_out, not_213_out, not_214_out, not_215_out, not_216_out, not_217_out,
       not_218_out, not_219_out, not_220_out, not_221_out, not_222_out, not_223_out, not_224_out,
       not_225_out, not_226_out, not_227_out, not_228_out, not_229_out, not_230_out, not_231_out,
       not_232_out, not_233_out, not_234_out, not_235_out, not_236_out, not_237_out, not_238_out,
       not_239_out, not_240_out, not_241_out, not_242_out, not_243_out, not_244_out, not_245_out,
       not_246_out, not_247_out, not_248_out, not_249_out, not_250_out, not_251_out, not_252_out,
       not_253_out, not_254_out, not_255_out, not_256_out, not_257_out, not_258_out, not_259_out,
       not_260_out, not_261_out, not_262_out, not_263_out, not_264_out, not_265_out, not_266_out,
       not_267_out, not_268_out, not_269_out, not_270_out, not_271_out, not_272_out, not_273_out,
       not_274_out, not_275_out, not_276_out, not_277_out, not_278_out, not_279_out, not_280_out,
       not_281_out, not_282_out, not_283_out, not_284_out, not_285_out, not_286_out, not_287_out,
       not_288_out, not_289_out, not_290_out, not_291_out, not_292_out, not_293_out, not_294_out,
       not_295_out, not_296_out, not_297_out, not_298_out, not_299_out, not_300_out, not_301_out,
       not_302_out, not_303_out, not_304_out, not_305_out, not_306_out;

  not not_1 (not_1_out, OP5);
  not not_2 (not_2_out, OP4);
  not not_3 (not_3_out, OP3);
  not not_4 (not_4_out, OP2);
  not not_5 (not_5_out, OP1);
  not not_6 (not_6_out, OP0);
  not not_7 (not_7_out, F5);
  not not_8 (not_8_out, F4);
  not not_9 (not_9_out, F3);
  not not_10 (not_10_out, F2);
  not not_11 (not_11_out, OP5);
  not not_12 (not_12_out, OP4);
  not not_13 (not_13_out, OP3);
  not not_14 (not_14_out, OP2);
  not not_15 (not_15_out, OP1);
  not not_16 (not_16_out, OP0);
  not not_17 (not_17_out, F4);
  not not_18 (not_18_out, F3);
  not not_19 (not_19_out, F2);
  not not_20 (not_20_out, F1);
  not not_21 (not_21_out, F0);
  not not_22 (not_22_out, OP5);
  not not_23 (not_23_out, OP4);
  not not_24 (not_24_out, OP3);
  not not_25 (not_25_out, OP2);
  not not_26 (not_26_out, OP1);
  not not_27 (not_27_out, OP0);
  not not_28 (not_28_out, F4);
  not not_29 (not_29_out, F3);
  not not_30 (not_30_out, F2);
  not not_31 (not_31_out, F1);
  not not_32 (not_32_out, OP5);
  not not_33 (not_33_out, OP4);
  not not_34 (not_34_out, OP3);
  not not_35 (not_35_out, OP2);
  not not_36 (not_36_out, OP1);
  not not_37 (not_37_out, OP0);
  not not_38 (not_38_out, F4);
  not not_39 (not_39_out, F3);
  not not_40 (not_40_out, F1);
  not not_41 (not_41_out, F0);
  not not_42 (not_42_out, OP5);
  not not_43 (not_43_out, OP4);
  not not_44 (not_44_out, OP3);
  not not_45 (not_45_out, OP2);
  not not_46 (not_46_out, OP1);
  not not_47 (not_47_out, OP0);
  not not_48 (not_48_out, F4);
  not not_49 (not_49_out, F2);
  not not_50 (not_50_out, F0);
  not not_51 (not_51_out, OP5);
  not not_52 (not_52_out, OP4);
  not not_53 (not_53_out, OP3);
  not not_54 (not_54_out, OP1);
  not not_55 (not_55_out, OP0);
  not not_56 (not_56_out, OP5);
  not not_57 (not_57_out, OP4);
  not not_58 (not_58_out, OP3);
  not not_59 (not_59_out, OP1);
  not not_60 (not_60_out, OP5);
  not not_61 (not_61_out, OP4);
  not not_62 (not_62_out, OP2);
  not not_63 (not_63_out, OP1);
  not not_64 (not_64_out, OP0);
  not not_65 (not_65_out, OP5);
  not not_66 (not_66_out, OP4);
  not not_67 (not_67_out, OP1);
  not not_68 (not_68_out, OP0);
  not not_69 (not_69_out, OP5);
  not not_70 (not_70_out, OP4);
  not not_71 (not_71_out, OP2);
  not not_72 (not_72_out, OP1);
  not not_73 (not_73_out, OP5);
  not not_74 (not_74_out, OP4);
  not not_75 (not_75_out, OP2);
  not not_76 (not_76_out, OP0);
  not not_77 (not_77_out, OP4);
  not not_78 (not_78_out, OP3);
  not not_79 (not_79_out, OP2);
  not not_80 (not_80_out, OP4);
  not not_81 (not_81_out, OP2);
  not not_82 (not_82_out, OP5);
  not not_83 (not_83_out, OP4);
  not not_84 (not_84_out, OP3);
  not not_85 (not_85_out, OP2);
  not not_86 (not_86_out, OP1);
  not not_87 (not_87_out, OP0);
  not not_88 (not_88_out, F4);
  not not_89 (not_89_out, F3);
  not not_90 (not_90_out, F0);
  not not_91 (not_91_out, OP4);
  not not_92 (not_92_out, OP3);
  not not_93 (not_93_out, OP2);
  not not_94 (not_94_out, OP1);
  not not_95 (not_95_out, OP0);
  not not_96 (not_96_out, OP5);
  not not_97 (not_97_out, OP4);
  not not_98 (not_98_out, OP3);
  not not_99 (not_99_out, OP5);
  not not_100 (not_100_out, OP4);
  not not_101 (not_101_out, OP3);
  not not_102 (not_102_out, OP2);
  not not_103 (not_103_out, OP1);
  not not_104 (not_104_out, OP0);
  not not_105 (not_105_out, F5);
  not not_106 (not_106_out, F4);
  not not_107 (not_107_out, F3);
  not not_108 (not_108_out, F2);
  not not_109 (not_109_out, F0);
  not not_110 (not_110_out, OP5);
  not not_111 (not_111_out, OP4);
  not not_112 (not_112_out, OP3);
  not not_113 (not_113_out, OP2);
  not not_114 (not_114_out, OP1);
  not not_115 (not_115_out, OP0);
  not not_116 (not_116_out, F4);
  not not_117 (not_117_out, F3);
  not not_118 (not_118_out, F2);
  not not_119 (not_119_out, F0);
  not not_120 (not_120_out, OP5);
  not not_121 (not_121_out, OP4);
  not not_122 (not_122_out, OP3);
  not not_123 (not_123_out, OP2);
  not not_124 (not_124_out, OP1);
  not not_125 (not_125_out, OP0);
  not not_126 (not_126_out, F4);
  not not_127 (not_127_out, F3);
  not not_128 (not_128_out, F1);
  not not_129 (not_129_out, F0);
  not not_130 (not_130_out, OP5);
  not not_131 (not_131_out, OP4);
  not not_132 (not_132_out, OP3);
  not not_133 (not_133_out, OP2);
  not not_134 (not_134_out, OP1);
  not not_135 (not_135_out, OP0);
  not not_136 (not_136_out, F4);
  not not_137 (not_137_out, F3);
  not not_138 (not_138_out, OP5);
  not not_139 (not_139_out, OP4);
  not not_140 (not_140_out, OP3);
  not not_141 (not_141_out, OP2);
  not not_142 (not_142_out, OP1);
  not not_143 (not_143_out, OP0);
  not not_144 (not_144_out, F4);
  not not_145 (not_145_out, F2);
  not not_146 (not_146_out, F0);
  not not_147 (not_147_out, OP5);
  not not_148 (not_148_out, OP4);
  not not_149 (not_149_out, OP3);
  not not_150 (not_150_out, OP1);
  not not_151 (not_151_out, OP0);
  not not_152 (not_152_out, OP5);
  not not_153 (not_153_out, OP4);
  not not_154 (not_154_out, OP3);
  not not_155 (not_155_out, OP1);
  not not_156 (not_156_out, OP5);
  not not_157 (not_157_out, OP4);
  not not_158 (not_158_out, OP1);
  not not_159 (not_159_out, OP0);
  not not_160 (not_160_out, OP5);
  not not_161 (not_161_out, OP4);
  not not_162 (not_162_out, OP2);
  not not_163 (not_163_out, OP0);
  not not_164 (not_164_out, OP5);
  not not_165 (not_165_out, OP4);
  not not_166 (not_166_out, OP3);
  not not_167 (not_167_out, OP5);
  not not_168 (not_168_out, OP4);
  not not_169 (not_169_out, OP3);
  not not_170 (not_170_out, OP2);
  not not_171 (not_171_out, OP1);
  not not_172 (not_172_out, OP0);
  not not_173 (not_173_out, F4);
  not not_174 (not_174_out, F3);
  not not_175 (not_175_out, F2);
  not not_176 (not_176_out, F1);
  not not_177 (not_177_out, F0);
  not not_178 (not_178_out, OP5);
  not not_179 (not_179_out, OP4);
  not not_180 (not_180_out, OP3);
  not not_181 (not_181_out, OP2);
  not not_182 (not_182_out, OP1);
  not not_183 (not_183_out, OP0);
  not not_184 (not_184_out, F4);
  not not_185 (not_185_out, F3);
  not not_186 (not_186_out, F2);
  not not_187 (not_187_out, F1);
  not not_188 (not_188_out, OP5);
  not not_189 (not_189_out, OP4);
  not not_190 (not_190_out, OP3);
  not not_191 (not_191_out, OP2);
  not not_192 (not_192_out, OP1);
  not not_193 (not_193_out, OP0);
  not not_194 (not_194_out, F4);
  not not_195 (not_195_out, F3);
  not not_196 (not_196_out, F2);
  not not_197 (not_197_out, F0);
  not not_198 (not_198_out, OP5);
  not not_199 (not_199_out, OP4);
  not not_200 (not_200_out, OP3);
  not not_201 (not_201_out, OP2);
  not not_202 (not_202_out, OP1);
  not not_203 (not_203_out, OP0);
  not not_204 (not_204_out, F4);
  not not_205 (not_205_out, F3);
  not not_206 (not_206_out, F1);
  not not_207 (not_207_out, F0);
  not not_208 (not_208_out, OP5);
  not not_209 (not_209_out, OP4);
  not not_210 (not_210_out, OP3);
  not not_211 (not_211_out, OP2);
  not not_212 (not_212_out, OP1);
  not not_213 (not_213_out, OP0);
  not not_214 (not_214_out, F4);
  not not_215 (not_215_out, F2);
  not not_216 (not_216_out, OP5);
  not not_217 (not_217_out, OP4);
  not not_218 (not_218_out, OP2);
  not not_219 (not_219_out, OP1);
  not not_220 (not_220_out, OP0);
  not not_221 (not_221_out, OP5);
  not not_222 (not_222_out, OP4);
  not not_223 (not_223_out, OP1);
  not not_224 (not_224_out, OP0);
  not not_225 (not_225_out, OP5);
  not not_226 (not_226_out, OP4);
  not not_227 (not_227_out, OP2);
  not not_228 (not_228_out, OP1);
  not not_229 (not_229_out, OP4);
  not not_230 (not_230_out, OP3);
  not not_231 (not_231_out, OP2);
  not not_232 (not_232_out, OP4);
  not not_233 (not_233_out, OP2);
  not not_234 (not_234_out, OP5);
  not not_235 (not_235_out, OP4);
  not not_236 (not_236_out, OP2);
  not not_237 (not_237_out, OP4);
  not not_238 (not_238_out, OP3);
  not not_239 (not_239_out, OP2);
  not not_240 (not_240_out, OP1);
  not not_241 (not_241_out, OP0);
  not not_242 (not_242_out, OP5);
  not not_243 (not_243_out, OP4);
  not not_244 (not_244_out, OP3);
  not not_245 (not_245_out, OP2);
  not not_246 (not_246_out, OP1);
  not not_247 (not_247_out, OP0);
  not not_248 (not_248_out, F4);
  not not_249 (not_249_out, F3);
  not not_250 (not_250_out, F1);
  not not_251 (not_251_out, OP5);
  not not_252 (not_252_out, OP4);
  not not_253 (not_253_out, OP3);
  not not_254 (not_254_out, OP2);
  not not_255 (not_255_out, OP1);
  not not_256 (not_256_out, OP0);
  not not_257 (not_257_out, F4);
  not not_258 (not_258_out, F3);
  not not_259 (not_259_out, OP5);
  not not_260 (not_260_out, OP4);
  not not_261 (not_261_out, OP3);
  not not_262 (not_262_out, OP2);
  not not_263 (not_263_out, OP1);
  not not_264 (not_264_out, OP0);
  not not_265 (not_265_out, F4);
  not not_266 (not_266_out, F2);
  not not_267 (not_267_out, F0);
  not not_268 (not_268_out, OP5);
  not not_269 (not_269_out, OP4);
  not not_270 (not_270_out, OP3);
  not not_271 (not_271_out, OP2);
  not not_272 (not_272_out, OP1);
  not not_273 (not_273_out, OP0);
  not not_274 (not_274_out, F4);
  not not_275 (not_275_out, F2);
  not not_276 (not_276_out, OP5);
  not not_277 (not_277_out, OP4);
  not not_278 (not_278_out, OP3);
  not not_279 (not_279_out, OP1);
  not not_280 (not_280_out, OP0);
  not not_281 (not_281_out, OP5);
  not not_282 (not_282_out, OP4);
  not not_283 (not_283_out, OP3);
  not not_284 (not_284_out, OP1);
  not not_285 (not_285_out, OP5);
  not not_286 (not_286_out, OP4);
  not not_287 (not_287_out, OP2);
  not not_288 (not_288_out, OP0);
  not not_289 (not_289_out, OP5);
  not not_290 (not_290_out, OP4);
  not not_291 (not_291_out, OP1);
  not not_292 (not_292_out, OP5);
  not not_293 (not_293_out, OP4);
  not not_294 (not_294_out, OP3);
  not not_295 (not_295_out, OP2);
  not not_296 (not_296_out, OP1);
  not not_297 (not_297_out, OP0);
  not not_298 (not_298_out, F4);
  not not_299 (not_299_out, F3);
  not not_300 (not_300_out, F0);
  not not_301 (not_301_out, OP5);
  not not_302 (not_302_out, OP4);
  not not_303 (not_303_out, OP2);
  not not_304 (not_304_out, OP5);
  not not_305 (not_305_out, OP4);
  not not_306 (not_306_out, OP3);
  and and_1 (and_1_out, not_1_out, not_2_out, not_3_out, not_4_out, not_5_out, not_6_out, not_7_out, not_8_out, not_9_out, not_10_out, F1, F0);
  and and_2 (and_2_out, not_11_out, not_12_out, not_13_out, not_14_out, not_15_out, not_16_out, F5, not_17_out, not_18_out, not_19_out, not_20_out, not_21_out);
  and and_3 (and_3_out, not_22_out, not_23_out, not_24_out, not_25_out, not_26_out, not_27_out, F5, not_28_out, not_29_out, not_30_out, not_31_out, F0);
  and and_4 (and_4_out, not_32_out, not_33_out, not_34_out, not_35_out, not_36_out, not_37_out, F5, not_38_out, not_39_out, F2, not_40_out, not_41_out);
  and and_5 (and_5_out, not_42_out, not_43_out, not_44_out, not_45_out, not_46_out, not_47_out, F5, not_48_out, F3, not_49_out, F1, not_50_out);
  and and_6 (and_6_out, not_51_out, not_52_out, not_53_out, OP2, not_54_out, not_55_out);
  and and_7 (and_7_out, not_56_out, not_57_out, not_58_out, OP2, not_59_out, OP0);
  and and_8 (and_8_out, not_60_out, not_61_out, OP3, not_62_out, not_63_out, not_64_out);
  and and_9 (and_9_out, not_65_out, not_66_out, OP3, OP2, not_67_out, not_68_out);
  and and_10 (and_10_out, not_69_out, not_70_out, OP3, not_71_out, not_72_out, OP0);
  and and_11 (and_11_out, not_73_out, not_74_out, OP3, not_75_out, OP1, not_76_out);
  and and_12 (and_12_out, OP5, not_77_out, not_78_out, not_79_out, OP1, OP0);
  and and_13 (and_13_out, OP5, not_80_out, OP3, not_81_out, OP1, OP0);
  and and_14 (and_14_out, not_82_out, not_83_out, not_84_out, not_85_out, not_86_out, not_87_out, F5, not_88_out, not_89_out, F2, F1, not_90_out);
  and and_15 (and_15_out, OP5, not_91_out, not_92_out, not_93_out, not_94_out, not_95_out);
  and and_16 (and_16_out, not_96_out, not_97_out, not_98_out, OP2, OP1, OP0);
  and and_17 (and_17_out, not_99_out, not_100_out, not_101_out, not_102_out, not_103_out, not_104_out, not_105_out, not_106_out, not_107_out, not_108_out, F1, not_109_out);
  and and_18 (and_18_out, not_110_out, not_111_out, not_112_out, not_113_out, not_114_out, not_115_out, F5, not_116_out, not_117_out, not_118_out, F1, not_119_out);
  and and_19 (and_19_out, not_120_out, not_121_out, not_122_out, not_123_out, not_124_out, not_125_out, F5, not_126_out, not_127_out, F2, not_128_out, not_129_out);
  and and_20 (and_20_out, not_130_out, not_131_out, not_132_out, not_133_out, not_134_out, not_135_out, F5, not_136_out, not_137_out, F2, F1, F0);
  and and_21 (and_21_out, not_138_out, not_139_out, not_140_out, not_141_out, not_142_out, not_143_out, F5, not_144_out, F3, not_145_out, F1, not_146_out);
  and and_22 (and_22_out, not_147_out, not_148_out, not_149_out, OP2, not_150_out, not_151_out);
  and and_23 (and_23_out, not_152_out, not_153_out, not_154_out, OP2, not_155_out, OP0);
  and and_24 (and_24_out, not_156_out, not_157_out, OP3, OP2, not_158_out, not_159_out);
  and and_25 (and_25_out, not_160_out, not_161_out, OP3, not_162_out, OP1, not_163_out);
  and and_26 (and_26_out, not_164_out, not_165_out, not_166_out, OP2, OP1, OP0);
  and and_27 (and_27_out, not_167_out, not_168_out, not_169_out, not_170_out, not_171_out, not_172_out, F5, not_173_out, not_174_out, not_175_out, not_176_out, not_177_out);
  and and_28 (and_28_out, not_178_out, not_179_out, not_180_out, not_181_out, not_182_out, not_183_out, F5, not_184_out, not_185_out, not_186_out, not_187_out, F0);
  and and_29 (and_29_out, not_188_out, not_189_out, not_190_out, not_191_out, not_192_out, not_193_out, F5, not_194_out, not_195_out, not_196_out, F1, not_197_out);
  and and_30 (and_30_out, not_198_out, not_199_out, not_200_out, not_201_out, not_202_out, not_203_out, F5, not_204_out, not_205_out, F2, not_206_out, not_207_out);
  and and_31 (and_31_out, not_208_out, not_209_out, not_210_out, not_211_out, not_212_out, not_213_out, F5, not_214_out, F3, not_215_out, F1, F0);
  and and_32 (and_32_out, not_216_out, not_217_out, OP3, not_218_out, not_219_out, not_220_out);
  and and_33 (and_33_out, not_221_out, not_222_out, OP3, OP2, not_223_out, not_224_out);
  and and_34 (and_34_out, not_225_out, not_226_out, OP3, not_227_out, not_228_out, OP0);
  and and_35 (and_35_out, OP5, not_229_out, not_230_out, not_231_out, OP1, OP0);
  and and_36 (and_36_out, OP5, not_232_out, OP3, not_233_out, OP1, OP0);
  and and_37 (and_37_out, not_234_out, not_235_out, OP3, not_236_out, OP1, OP0);
  and and_38 (and_38_out, OP5, not_237_out, not_238_out, not_239_out, not_240_out, not_241_out);
  and and_39 (and_39_out, not_242_out, not_243_out, not_244_out, not_245_out, not_246_out, not_247_out, F5, not_248_out, not_249_out, F2, not_250_out, F0);
  and and_40 (and_40_out, not_251_out, not_252_out, not_253_out, not_254_out, not_255_out, not_256_out, F5, not_257_out, not_258_out, F2, F1, F0);
  and and_41 (and_41_out, not_259_out, not_260_out, not_261_out, not_262_out, not_263_out, not_264_out, F5, not_265_out, F3, not_266_out, F1, not_267_out);
  and and_42 (and_42_out, not_268_out, not_269_out, not_270_out, not_271_out, not_272_out, not_273_out, F5, not_274_out, F3, not_275_out, F1, F0);
  and and_43 (and_43_out, not_276_out, not_277_out, not_278_out, OP2, not_279_out, not_280_out);
  and and_44 (and_44_out, not_281_out, not_282_out, not_283_out, OP2, not_284_out, OP0);
  and and_45 (and_45_out, not_285_out, not_286_out, OP3, not_287_out, OP1, not_288_out);
  and and_46 (and_46_out, not_289_out, not_290_out, OP3, OP2, not_291_out, OP0);
  and and_47 (and_47_out, not_292_out, not_293_out, not_294_out, not_295_out, not_296_out, not_297_out, F5, not_298_out, not_299_out, F2, F1, not_300_out);
  and and_48 (and_48_out, not_301_out, not_302_out, OP3, not_303_out, OP1, OP0);
  and and_49 (and_49_out, not_304_out, not_305_out, not_306_out, OP2, OP1, OP0);
  or or_1 (S1, and_17_out, and_18_out, and_19_out, and_20_out, and_21_out, and_22_out, and_23_out, and_24_out, and_25_out, and_26_out);
  or or_2 (S3, and_39_out, and_40_out, and_41_out, and_42_out, and_43_out, and_44_out, and_45_out, and_46_out, and_47_out, and_48_out, and_49_out);
  or or_3 (S0, and_1_out, and_2_out, and_3_out, and_4_out, and_5_out, and_6_out, and_7_out, and_8_out, and_9_out, and_10_out, and_11_out, and_12_out, and_13_out, and_14_out, and_15_out, and_16_out);
  or or_4 (S2, and_27_out, and_28_out, and_29_out, and_30_out, and_31_out, and_32_out, and_33_out, and_34_out, and_35_out, and_36_out, and_37_out, and_38_out);
endmodule

// 控制信号生成
module \控制信号自动生成  (
  input  OP0,
  input  OP1,
  input  OP2,
  input  OP3,
  input  OP4,
  input  OP5,
  input  F0,
  input  F1,
  input  F2,
  input  F3,
  input  F4,
  input  F5,
  output MemToReg,
  output MemWrite,
  output ALU_SRC,
  output RegWrite,
  output SysCALL,
  output SignedExt,
  output RegDst,
  output BEQ,
  output BNE,
  output JR,
  output JUMP,
  output JAL,
  output BGTZ,
  output LB
);

  wire and_1_out, and_2_out, and_4_out, and_5_out, and_6_out, and_7_out, and_8_out, and_9_out, and_10_out,
       and_11_out, and_12_out, and_13_out, and_14_out, and_15_out, and_16_out, and_18_out, and_19_out,
       and_20_out, and_21_out, and_22_out, and_23_out, and_24_out, and_25_out, and_26_out, and_27_out,
       and_28_out, not_1_out, not_2_out, not_3_out, not_4_out, not_5_out, not_6_out, not_7_out, not_8_out,
       not_9_out, not_10_out, not_11_out, not_12_out, not_13_out, not_14_out, not_15_out, not_16_out,
       not_17_out, not_18_out, not_19_out, not_20_out, not_21_out, not_22_out, not_23_out, not_24_out,
       not_25_out, not_26_out, not_27_out, not_28_out, not_29_out, not_30_out, not_31_out, not_32_out,
       not_33_out, not_34_out, not_35_out, not_36_out, not_37_out, not_38_out, not_39_out, not_40_out,
       not_41_out, not_42_out, not_43_out, not_44_out, not_45_out, not_46_out, not_47_out, not_48_out,
       not_49_out, not_50_out, not_51_out, not_52_out, not_53_out, not_54_out, not_55_out, not_56_out,
       not_57_out, not_58_out, not_59_out, not_60_out, not_61_out, not_62_out, not_63_out, not_64_out,
       not_65_out, not_66_out, not_67_out, not_68_out, not_69_out, not_70_out, not_71_out, not_72_out,
       not_73_out, not_74_out, not_75_out, not_76_out, not_77_out, not_78_out, not_79_out, not_80_out,
       not_81_out, not_82_out, not_83_out, not_84_out, not_85_out, not_86_out, not_87_out, not_88_out,
       not_89_out, not_90_out, not_91_out, not_92_out, not_93_out, not_94_out, not_95_out, not_96_out,
       not_97_out, not_98_out, not_99_out, not_100_out, not_101_out, not_102_out, not_103_out, not_104_out,
       not_105_out, not_106_out, not_107_out, not_108_out, not_109_out, not_110_out, not_111_out,
       not_112_out, not_113_out, not_114_out, not_115_out, not_116_out, not_117_out, not_118_out,
       not_119_out, not_120_out, not_121_out, not_122_out, not_123_out, not_124_out, not_125_out,
       not_126_out, not_127_out, not_128_out, not_129_out, not_130_out, not_131_out, not_132_out,
       not_133_out, not_134_out, not_135_out, not_136_out, not_137_out, not_138_out, not_139_out,
       not_140_out, not_141_out, not_142_out, not_143_out, not_144_out, not_145_out, not_146_out,
       not_147_out, not_148_out, not_149_out, not_150_out, not_151_out, not_152_out, not_153_out,
       not_154_out, not_155_out, not_156_out, not_157_out, not_158_out, not_159_out, not_160_out,
       not_161_out, not_162_out, not_163_out, not_164_out, not_165_out, not_166_out, not_167_out,
       not_168_out, not_169_out, not_170_out, not_171_out, not_172_out, not_173_out, not_174_out,
       not_175_out, not_176_out, not_177_out, not_178_out, not_179_out, not_180_out, not_181_out,
       not_182_out, not_183_out, not_184_out, not_185_out, not_186_out, not_187_out, not_188_out,
       not_189_out, not_190_out, not_191_out, not_192_out, not_193_out, not_194_out, not_195_out,
       not_196_out, not_197_out, not_198_out, not_199_out;

  not not_1 (not_1_out, OP0);
  not not_2 (not_2_out, OP1);
  not not_3 (not_3_out, OP2);
  not not_4 (not_4_out, OP3);
  not not_5 (not_5_out, OP4);
  not not_6 (not_6_out, OP2);
  not not_7 (not_7_out, OP3);
  not not_8 (not_8_out, OP4);
  not not_9 (not_9_out, OP2);
  not not_10 (not_10_out, OP4);
  not not_11 (not_11_out, OP0);
  not not_12 (not_12_out, OP1);
  not not_13 (not_13_out, OP2);
  not not_14 (not_14_out, OP3);
  not not_15 (not_15_out, OP4);
  not not_16 (not_16_out, OP1);
  not not_17 (not_17_out, OP4);
  not not_18 (not_18_out, OP5);
  not not_19 (not_19_out, OP2);
  not not_20 (not_20_out, OP4);
  not not_21 (not_21_out, OP5);
  not not_22 (not_22_out, OP2);
  not not_23 (not_23_out, OP4);
  not not_24 (not_24_out, OP0);
  not not_25 (not_25_out, OP1);
  not not_26 (not_26_out, OP2);
  not not_27 (not_27_out, OP3);
  not not_28 (not_28_out, OP4);
  not not_29 (not_29_out, F0);
  not not_30 (not_30_out, F2);
  not not_31 (not_31_out, F3);
  not not_32 (not_32_out, F4);
  not not_33 (not_33_out, OP0);
  not not_34 (not_34_out, OP1);
  not not_35 (not_35_out, OP2);
  not not_36 (not_36_out, OP3);
  not not_37 (not_37_out, OP4);
  not not_38 (not_38_out, F1);
  not not_39 (not_39_out, F3);
  not not_40 (not_40_out, F4);
  not not_41 (not_41_out, OP0);
  not not_42 (not_42_out, OP1);
  not not_43 (not_43_out, OP2);
  not not_44 (not_44_out, OP3);
  not not_45 (not_45_out, OP4);
  not not_46 (not_46_out, F3);
  not not_47 (not_47_out, F4);
  not not_48 (not_48_out, OP0);
  not not_49 (not_49_out, OP1);
  not not_50 (not_50_out, OP2);
  not not_51 (not_51_out, OP3);
  not not_52 (not_52_out, OP4);
  not not_53 (not_53_out, F2);
  not not_54 (not_54_out, F3);
  not not_55 (not_55_out, F4);
  not not_56 (not_56_out, F5);
  not not_57 (not_57_out, OP0);
  not not_58 (not_58_out, OP1);
  not not_59 (not_59_out, OP2);
  not not_60 (not_60_out, OP3);
  not not_61 (not_61_out, OP4);
  not not_62 (not_62_out, F2);
  not not_63 (not_63_out, F4);
  not not_64 (not_64_out, OP0);
  not not_65 (not_65_out, OP1);
  not not_66 (not_66_out, OP2);
  not not_67 (not_67_out, OP3);
  not not_68 (not_68_out, OP4);
  not not_69 (not_69_out, OP1);
  not not_70 (not_70_out, OP4);
  not not_71 (not_71_out, OP5);
  not not_72 (not_72_out, OP2);
  not not_73 (not_73_out, OP4);
  not not_74 (not_74_out, OP5);
  not not_75 (not_75_out, OP2);
  not not_76 (not_76_out, OP3);
  not not_77 (not_77_out, OP4);
  not not_78 (not_78_out, OP0);
  not not_79 (not_79_out, OP1);
  not not_80 (not_80_out, OP2);
  not not_81 (not_81_out, OP3);
  not not_82 (not_82_out, OP4);
  not not_83 (not_83_out, OP5);
  not not_84 (not_84_out, F0);
  not not_85 (not_85_out, F1);
  not not_86 (not_86_out, F4);
  not not_87 (not_87_out, F5);
  not not_88 (not_88_out, OP0);
  not not_89 (not_89_out, OP1);
  not not_90 (not_90_out, OP2);
  not not_91 (not_91_out, OP3);
  not not_92 (not_92_out, OP4);
  not not_93 (not_93_out, OP0);
  not not_94 (not_94_out, OP2);
  not not_95 (not_95_out, OP4);
  not not_96 (not_96_out, OP5);
  not not_97 (not_97_out, OP1);
  not not_98 (not_98_out, OP2);
  not not_99 (not_99_out, OP4);
  not not_100 (not_100_out, OP5);
  not not_101 (not_101_out, OP1);
  not not_102 (not_102_out, OP3);
  not not_103 (not_103_out, OP4);
  not not_104 (not_104_out, OP5);
  not not_105 (not_105_out, OP2);
  not not_106 (not_106_out, OP4);
  not not_107 (not_107_out, OP0);
  not not_108 (not_108_out, OP1);
  not not_109 (not_109_out, OP2);
  not not_110 (not_110_out, OP3);
  not not_111 (not_111_out, OP4);
  not not_112 (not_112_out, OP5);
  not not_113 (not_113_out, F0);
  not not_114 (not_114_out, F1);
  not not_115 (not_115_out, F2);
  not not_116 (not_116_out, F4);
  not not_117 (not_117_out, F5);
  not not_118 (not_118_out, OP0);
  not not_119 (not_119_out, OP1);
  not not_120 (not_120_out, OP2);
  not not_121 (not_121_out, OP3);
  not not_122 (not_122_out, OP4);
  not not_123 (not_123_out, OP5);
  not not_124 (not_124_out, F0);
  not not_125 (not_125_out, F2);
  not not_126 (not_126_out, F3);
  not not_127 (not_127_out, F4);
  not not_128 (not_128_out, OP0);
  not not_129 (not_129_out, OP1);
  not not_130 (not_130_out, OP2);
  not not_131 (not_131_out, OP3);
  not not_132 (not_132_out, OP4);
  not not_133 (not_133_out, OP5);
  not not_134 (not_134_out, F1);
  not not_135 (not_135_out, F3);
  not not_136 (not_136_out, F4);
  not not_137 (not_137_out, OP0);
  not not_138 (not_138_out, OP1);
  not not_139 (not_139_out, OP2);
  not not_140 (not_140_out, OP3);
  not not_141 (not_141_out, OP4);
  not not_142 (not_142_out, OP5);
  not not_143 (not_143_out, F3);
  not not_144 (not_144_out, F4);
  not not_145 (not_145_out, OP0);
  not not_146 (not_146_out, OP1);
  not not_147 (not_147_out, OP2);
  not not_148 (not_148_out, OP3);
  not not_149 (not_149_out, OP4);
  not not_150 (not_150_out, OP5);
  not not_151 (not_151_out, F2);
  not not_152 (not_152_out, F3);
  not not_153 (not_153_out, F4);
  not not_154 (not_154_out, F5);
  not not_155 (not_155_out, OP0);
  not not_156 (not_156_out, OP1);
  not not_157 (not_157_out, OP2);
  not not_158 (not_158_out, OP3);
  not not_159 (not_159_out, OP4);
  not not_160 (not_160_out, OP5);
  not not_161 (not_161_out, F2);
  not not_162 (not_162_out, F4);
  not not_163 (not_163_out, OP0);
  not not_164 (not_164_out, OP1);
  not not_165 (not_165_out, OP3);
  not not_166 (not_166_out, OP4);
  not not_167 (not_167_out, OP5);
  not not_168 (not_168_out, OP1);
  not not_169 (not_169_out, OP3);
  not not_170 (not_170_out, OP4);
  not not_171 (not_171_out, OP5);
  not not_172 (not_172_out, OP0);
  not not_173 (not_173_out, OP1);
  not not_174 (not_174_out, OP2);
  not not_175 (not_175_out, OP3);
  not not_176 (not_176_out, OP4);
  not not_177 (not_177_out, OP5);
  not not_178 (not_178_out, F0);
  not not_179 (not_179_out, F1);
  not not_180 (not_180_out, F2);
  not not_181 (not_181_out, F4);
  not not_182 (not_182_out, F5);
  not not_183 (not_183_out, OP0);
  not not_184 (not_184_out, OP2);
  not not_185 (not_185_out, OP3);
  not not_186 (not_186_out, OP4);
  not not_187 (not_187_out, OP5);
  not not_188 (not_188_out, OP2);
  not not_189 (not_189_out, OP3);
  not not_190 (not_190_out, OP4);
  not not_191 (not_191_out, OP5);
  not not_192 (not_192_out, OP3);
  not not_193 (not_193_out, OP4);
  not not_194 (not_194_out, OP5);
  not not_195 (not_195_out, OP4);
  not not_196 (not_196_out, OP3);
  not not_197 (not_197_out, OP2);
  not not_198 (not_198_out, OP1);
  not not_199 (not_199_out, OP0);
  and and_1 (and_1_out, not_1_out, not_2_out, not_3_out, not_4_out, not_5_out, OP5);
  and and_2 (and_2_out, OP0, OP1, not_6_out, not_7_out, not_8_out, OP5);
  and and_3 (MemWrite, OP0, OP1, not_9_out, OP3, not_10_out, OP5);
  and and_4 (and_4_out, not_11_out, not_12_out, not_13_out, not_14_out, not_15_out, OP5);
  and and_5 (and_5_out, not_16_out, OP3, not_17_out, not_18_out);
  and and_6 (and_6_out, not_19_out, OP3, not_20_out, not_21_out);
  and and_7 (and_7_out, OP0, OP1, not_22_out, not_23_out);
  and and_8 (and_8_out, not_24_out, not_25_out, not_26_out, not_27_out, not_28_out, not_29_out, not_30_out, not_31_out, not_32_out);
  and and_9 (and_9_out, not_33_out, not_34_out, not_35_out, not_36_out, not_37_out, not_38_out, not_39_out, not_40_out, F5);
  and and_10 (and_10_out, not_41_out, not_42_out, not_43_out, not_44_out, not_45_out, F2, not_46_out, not_47_out, F5);
  and and_11 (and_11_out, not_48_out, not_49_out, not_50_out, not_51_out, not_52_out, F1, not_53_out, not_54_out, not_55_out, not_56_out);
  and and_12 (and_12_out, not_57_out, not_58_out, not_59_out, not_60_out, not_61_out, F1, not_62_out, F3, not_63_out, F5);
  and and_13 (and_13_out, not_64_out, not_65_out, not_66_out, not_67_out, not_68_out, OP5);
  and and_14 (and_14_out, not_69_out, OP3, not_70_out, not_71_out);
  and and_15 (and_15_out, not_72_out, OP3, not_73_out, not_74_out);
  and and_16 (and_16_out, OP0, OP1, not_75_out, not_76_out, not_77_out);
  and and_17 (SysCALL, not_78_out, not_79_out, not_80_out, not_81_out, not_82_out, not_83_out, not_84_out, not_85_out, F2, F3, not_86_out, not_87_out);
  and and_18 (and_18_out, not_88_out, not_89_out, not_90_out, not_91_out, not_92_out, OP5);
  and and_19 (and_19_out, not_93_out, not_94_out, OP3, not_95_out, not_96_out);
  and and_20 (and_20_out, not_97_out, not_98_out, OP3, not_99_out, not_100_out);
  and and_21 (and_21_out, not_101_out, OP2, not_102_out, not_103_out, not_104_out);
  and and_22 (and_22_out, OP0, OP1, not_105_out, not_106_out, OP5);
  and and_23 (and_23_out, not_107_out, not_108_out, not_109_out, not_110_out, not_111_out, not_112_out, not_113_out, not_114_out, not_115_out, not_116_out, not_117_out);
  and and_24 (and_24_out, not_118_out, not_119_out, not_120_out, not_121_out, not_122_out, not_123_out, not_124_out, not_125_out, not_126_out, not_127_out);
  and and_25 (and_25_out, not_128_out, not_129_out, not_130_out, not_131_out, not_132_out, not_133_out, not_134_out, not_135_out, not_136_out, F5);
  and and_26 (and_26_out, not_137_out, not_138_out, not_139_out, not_140_out, not_141_out, not_142_out, F2, not_143_out, not_144_out, F5);
  and and_27 (and_27_out, not_145_out, not_146_out, not_147_out, not_148_out, not_149_out, not_150_out, F1, not_151_out, not_152_out, not_153_out, not_154_out);
  and and_28 (and_28_out, not_155_out, not_156_out, not_157_out, not_158_out, not_159_out, not_160_out, F1, not_161_out, F3, not_162_out, F5);
  and and_29 (BEQ, not_163_out, not_164_out, OP2, not_165_out, not_166_out, not_167_out);
  and and_30 (BNE, OP0, not_168_out, OP2, not_169_out, not_170_out, not_171_out);
  and and_31 (JR, not_172_out, not_173_out, not_174_out, not_175_out, not_176_out, not_177_out, not_178_out, not_179_out, not_180_out, F3, not_181_out, not_182_out);
  and and_32 (JUMP, not_183_out, OP1, not_184_out, not_185_out, not_186_out, not_187_out);
  and and_33 (JAL, OP0, OP1, not_188_out, not_189_out, not_190_out, not_191_out);
  and and_34 (BGTZ, OP0, OP1, OP2, not_192_out, not_193_out, not_194_out);
  and and_35 (LB, OP5, not_195_out, not_196_out, not_197_out, not_198_out, not_199_out);
  or or_1 (MemToReg, and_1_out, and_2_out);
  or or_2 (ALU_SRC, and_4_out, and_5_out, and_6_out, and_7_out);
  or or_3 (RegWrite, and_8_out, and_9_out, and_10_out, and_11_out, and_12_out, and_13_out, and_14_out, and_15_out, and_16_out);
  or or_4 (SignedExt, and_18_out, and_19_out, and_20_out, and_21_out, and_22_out);
  or or_5 (RegDst, and_23_out, and_24_out, and_25_out, and_26_out, and_27_out, and_28_out);
endmodule

// ALU
module MIPS_ALU (
  input  [4:0] shamt,
  input  [31:0] X,
  input  [31:0] Y,
  input  [3:0] AluOP,
  output Equal,
  output [31:0] Result,
  output [31:0] Result_2
);

  wire [0:0] comparator_1_lt, comparator_2_lt;
  wire [31:0] adder_1_out, AND_out, divider_1_out, divider_1_rem, multiplier_1_cout, multiplier_1_out,
       NOR_out, OR_out, shifter_1_out, shifter_2_out, shifter_3_out, subtractor_1_out, XOR_out;

  assign AND_out = X & Y;  // AND_Gate AND, 32 bits wide
  assign OR_out = X | Y;  // OR_Gate OR, 32 bits wide
  Shifter #(.width(32), .shift("ll")) shifter_1 (.in(Y), .\dist (shamt), .out(shifter_1_out));
  Shifter #(.width(32), .shift("ar")) shifter_2 (.in(Y), .\dist (shamt), .out(shifter_2_out));
  Shifter #(.width(32), .shift("lr")) shifter_3 (.in(Y), .\dist (shamt), .out(shifter_3_out));
  Multiplier #(.width(32)) multiplier_1 (.a(X), .b(Y), .out(multiplier_1_out), .cout(multiplier_1_cout));  // open: cin
  Divider #(.width(32)) divider_1 (.a(X), .b(Y), .out(divider_1_out), .rem(divider_1_rem));  // open: upper
  Adder #(.width(32)) adder_1 (.a(X), .b(Y), .out(adder_1_out));  // open: cin, cout
  Subtractor #(.width(32)) subtractor_1 (.a(X), .b(Y), .out(subtractor_1_out));  // open: bin, bout
  assign XOR_out = X ^ Y;  // XOR_Gate XOR, 32 bits wide
  assign NOR_out = ~(X | Y);  // NOR_Gate NOR, 32 bits wide
  Comparator #(.width(32), .mode("twosComplement")) comparator_1 (
    .a(X), .b(Y), .eq(Equal), .lt(comparator_1_lt[0]));  // open: gt
  Comparator #(.width(32), .mode("unsigned")) comparator_2 (.a(X), .b(Y), .lt(comparator_2_lt[0]));  // open: gt, eq
  Multiplexer #(.select(4), .width(32), .disabled("Z"), .enable("false")) multiplexer_1 (
    .in0(shifter_1_out), .in1(shifter_2_out), .in2(shifter_3_out), .in3(multiplier_1_out),
    .in4(divider_1_out), .in5(adder_1_out), .in6(subtractor_1_out), .in7(AND_out), .in8(OR_out),
    .in9(XOR_out), .in10(NOR_out), .in11({{31{1'b0}}, comparator_1_lt[0]}),
    .in12({{31{1'b0}}, comparator_2_lt[0]}), .in13({32{1'b0}}), .in14({32{1'b0}}), .in15({32{1'b0}}),
    .out(Result), .sel(AluOP));
  Multiplexer #(.select(4), .width(32), .disabled("Z"), .enable("false")) multiplexer_2 (
    .in0({32{1'b0}}), .in1({32{1'b0}}), .in2({32{1'b0}}), .in3(multiplier_1_cout), .in4(divider_1_rem),
    .in5({32{1'b0}}), .in6({32{1'b0}}), .in7({32{1'b0}}), .in8({32{1'b0}}), .in9({32{1'b0}}),
    .in10({32{1'b0}}), .in11({32{1'b0}}), .in12({32{1'b0}}), .in13({32{1'b0}}), .in14({32{1'b0}}),
    .in15({32{1'b0}}), .out(Result_2), .sel(AluOP));

  // Other names for the same wires on the sheet: Result2[31:0] = Result_2; S[3:0] = AluOP

  // Notes on the sheet:
  //   不要改变此引脚区域内容，也不要改变ALU封装形式
  //   输入引脚
  //   输出引脚
endmodule

module MIPS_Regifile (
  input  [31:0] Din,
  input  Clk,
  input  WE,
  input  [4:0] R1_num,
  input  [4:0] W_num,
  input  [4:0] R2_num,
  output [31:0] R1,
  output [31:0] R2
);

  // RegisterFile registerfile_1: pin names not known; wires that end beside it: Din, Clk, WE, W_num, R1_num, R2_num, R1, R2
endmodule

module \理想流水线  (
);

  wire CLK, Go, IR1, IR2, IR3, RST, W1, W2, W3;
  wire [11:0] EX_PC, ID_PC, IF_PC, MEM_PC, WB_PC;
  wire [15:0] \LoadUse次数 , \总周期数 , \插入气泡数 , \无条件分支数 , \条件分支成功数 ;
  wire [31:0] LedData;

  Button \u_总复位  (.out(RST));
  Button _1 (.out(IR1));
  Button _2 (.out(IR2));
  Button _3 (.out(IR3));
  Button \u_继续运行  (.out(Go));
  LED #(.active("true")) led_1 (.in(W1));
  LED #(.active("true")) led_2 (.in(W2));
  LED #(.active("true")) led_3 (.in(W3));
  Hex_Digit_Display hex_digit_display_1 (.value(LedData[31:28]));  // open: dp
  Hex_Digit_Display hex_digit_display_2 (.value(LedData[27:24]));  // open: dp
  Hex_Digit_Display hex_digit_display_3 (.value(LedData[23:20]));  // open: dp
  Hex_Digit_Display hex_digit_display_4 (.value(LedData[15:12]));  // open: dp
  Hex_Digit_Display hex_digit_display_5 (.value(LedData[19:16]));  // open: dp
  Hex_Digit_Display hex_digit_display_6 (.value(LedData[7:4]));  // open: dp
  Hex_Digit_Display hex_digit_display_7 (.value(LedData[11:8]));  // open: dp
  Clock #(.highDuration(1), .lowDuration(1)) clock_1 (.out(CLK));
  Hex_Digit_Display hex_digit_display_8 (.value(LedData[3:0]));  // open: dp
  // Probe on \总周期数 
  // Probe on \无条件分支数 
  // Probe on \条件分支成功数 
  // Probe on \插入气泡数 
  // Probe on \LoadUse次数 
  // Probe on IF_PC
  // Probe on EX_PC
  // Probe on ID_PC
  // Probe on MEM_PC
  // Probe on WB_PC

  // Notes on the sheet:
  //   中断源
  //   中断等待指示
  //   数码管输出
  //   流水调试日志用
endmodule

module \气泡流水线  (
  output RegWrite,
  output MemWrite,
  output [31:0] PC,
  output [31:0] IR,
  output [31:0] RDin,
  output [31:0] MDin
);

  wire CLK, Go, IR1, IR2, IR3, W1, W2, W3;
  wire [15:0] \总周期数 ;
  wire [31:0] LedData;

  Clock #(.highDuration(1), .lowDuration(1)) clock_1 (.out(CLK));
  Button _1 (.out(IR1));
  Button _2 (.out(IR2));
  Button _3 (.out(IR3));
  Button \u_继续运行  (.out(Go));
  LED #(.active("true")) led_1 (.in(W1));
  LED #(.active("true")) led_2 (.in(W2));
  LED #(.active("true")) led_3 (.in(W3));
  Hex_Digit_Display hex_digit_display_1 (.value(LedData[31:28]));  // open: dp
  Hex_Digit_Display hex_digit_display_2 (.value(LedData[23:20]));  // open: dp
  Hex_Digit_Display hex_digit_display_3 (.value(LedData[27:24]));  // open: dp
  Hex_Digit_Display hex_digit_display_4 (.value(LedData[15:12]));  // open: dp
  Hex_Digit_Display hex_digit_display_5 (.value(LedData[19:16]));  // open: dp
  Hex_Digit_Display hex_digit_display_6 (.value(LedData[11:8]));  // open: dp
  Hex_Digit_Display hex_digit_display_7 (.value(LedData[7:4]));  // open: dp
  // Probe on \总周期数 
  Hex_Digit_Display hex_digit_display_8 (.value(LedData[3:0]));  // open: dp

  // Notes on the sheet:
  //   中断源
  //   中断等待指示
  //   总复位信号应将除ROM以外所有存储组件全部清零
  //   数码管输出
  //   数码管输出应该用寄存器锁存，否则显示数据只能一闪而过
  //   为方便自动评测，需要输出PC，IR，寄存器文件写入端口RDin，内存写入端口MDin等信号
endmodule

module \重定向流水线  (
  output RegWrite,
  output MemWrite,
  output [31:0] PC,
  output [31:0] IR,
  output [31:0] RDin,
  output [31:0] MDin
);

  wire CLK, Go, IR1, IR2, IR3, W1, W2, W3;
  wire [15:0] \总周期数 ;
  wire [31:0] LedData;

  Clock #(.highDuration(1), .lowDuration(1)) clock_1 (.out(CLK));
  Button _1 (.out(IR1));
  Button _2 (.out(IR2));
  Button _3 (.out(IR3));
  Button \u_继续运行  (.out(Go));
  LED #(.active("true")) led_1 (.in(W1));
  LED #(.active("true")) led_2 (.in(W2));
  LED #(.active("true")) led_3 (.in(W3));
  Hex_Digit_Display hex_digit_display_1 (.value(LedData[31:28]));  // open: dp
  Hex_Digit_Display hex_digit_display_2 (.value(LedData[23:20]));  // open: dp
  Hex_Digit_Display hex_digit_display_3 (.value(LedData[27:24]));  // open: dp
  Hex_Digit_Display hex_digit_display_4 (.value(LedData[15:12]));  // open: dp
  Hex_Digit_Display hex_digit_display_5 (.value(LedData[19:16]));  // open: dp
  Hex_Digit_Display hex_digit_display_6 (.value(LedData[7:4]));  // open: dp
  Hex_Digit_Display hex_digit_display_7 (.value(LedData[11:8]));  // open: dp
  // Probe on \总周期数 
  Hex_Digit_Display hex_digit_display_8 (.value(LedData[3:0]));  // open: dp

  // Notes on the sheet:
  //   中断源
  //   中断等待指示
  //   总复位信号应将除ROM以外所有存储组件全部清零
  //   数码管输出
  //   数码管输出应该用寄存器锁存，否则显示数据只能一闪而过
  //   为方便自动评测，需要输出PC，IR，寄存器文件写入端口RDin，内存写入端口MDin等信号
endmodule

module \中断按键参考电路  (
  input  \同步清零信号 ,
  output \与中断屏蔽位与 
);

  wire \_1号中断_out , and_1_out, clock_1_out, d_ff_1_q, or_1_out, or_2_out;

  Clock #(.highDuration(1), .lowDuration(1)) clock_1 (.out(clock_1_out));
  Button \_1号中断  (.out(\_1号中断_out ));
  or or_1 (or_1_out, \与中断屏蔽位与 , d_ff_1_q);
  LED #(.active("true")) \_1号中断等待指示灯  (.in(or_1_out));
  D_Flip_Flop #(.trigger("rising"), .Pre_Clr_Positions("LEGACY"), .NegatePresetClear("false"), .enable("true"), .NewFFLayout("false")) d_ff_1 (
    .clk(\_1号中断_out ), .D(1'b1), .Q(d_ff_1_q), .reset(\与中断屏蔽位与 ));  // open: Qn, preset, en
  or or_2 (or_2_out, d_ff_1_q, \与中断屏蔽位与 );
  and and_1 (and_1_out, or_2_out, ~\同步清零信号 );  // AND_Gate
  D_Flip_Flop #(.trigger("rising"), .Pre_Clr_Positions("LEGACY"), .NegatePresetClear("false"), .enable("true"), .NewFFLayout("false")) IR1 (
    .clk(clock_1_out), .D(and_1_out), .Q(\与中断屏蔽位与 ));  // open: Qn, preset, en, reset
  \单周期硬布线控制器  \u_单周期硬布线控制器_1  ();  // open: Func, OP, ALU_OP, MemToReg, MemWrite, ALU_SRC, RegWrite, SysCALL, SignedExt, RegDst, JR, JMP, Beq, JAL, Bne, BGTZ, LB

  // Notes on the sheet:
  //   中断信号采样参考电路
  //   Reset 
endmodule

module \确定pc  (
  input  equal,
  input  Beq,
  input  Bne,
  input  JR,
  input  j,
  output beq_bne_suc,
  output [1:0] out_7
);

  wire and_1_out, and_2_out, and_3_out, and_4_out, and_5_out, not_1_out, not_2_out, or_1_out, or_2_out;
  wire [1:1] or_4_out;

  or or_1 (or_1_out, Beq, Bne);
  and and_1 (and_1_out, equal, or_1_out);
  or or_2 (or_2_out, Beq, and_1_out, Bne, JR, j);
  not not_1 (not_1_out, and_1_out);
  not not_2 (not_2_out, or_2_out);
  and and_2 (and_2_out, and_1_out, Beq);
  and and_3 (and_3_out, not_1_out, Bne);
  and and_4 (and_4_out, Beq, not_1_out);
  and and_5 (and_5_out, Bne, and_1_out);
  or or_3 (beq_bne_suc, and_2_out, and_3_out);
  or or_4 (or_4_out[1], and_4_out, not_2_out, and_5_out);
  Multiplexer #(.select(4), .width(2), .disabled("Z"), .enable("false")) multiplexer_1 (
    .in1(2'b00), .in2(2'b01), .in4(2'b10), .in8(2'b11), .out(out_7), .sel({j, JR, or_4_out[1], beq_bne_suc}));  // open: in0, in3, in5, in6, in7, in9, in10, in11, in12, in13, in14, in15
endmodule
